# Fritzing sketch StanBaseBBPico (saved by Fritzing 0.9.6b)

parts:
  Arduino_Nano = Arduino Nano (Rev3.0)
  A4988_Board = Pololu A4988 [package=SO16]
  A4988_Board_2 = Pololu A4988 [package=SO16]
  R1 = Resistor [tolerance=±5% resistance=62k power=0.25 package=THT]
  R2 = Resistor [tolerance=±5% resistance=100k power=0.25 package=THT]
  C3 = Electrolytic Capacitor [capacitance=100µF voltage=50V package="200 mil [THT, electrolytic]"]
  C4 = Electrolytic Capacitor [capacitance=100µF voltage=50V package="200 mil [THT, electrolytic]"]
  Right_Motor = Header 4 [package=jst-4-pth]
  Left_Motor = Header 4 [package=jst-4-pth]
  Power_SW/BAT_(LiPo3S) = Header 2 [package=jst-2-pth]
  JP1 = Header 6 [package=molex-1x6_lock]
  Tilt_Servo = Header 3 [package=molex-1x3_lock]
  Pan_Servo = Header 3 [package=molex-1x3_lock]
  Led_Matrix = Header 3 [package=molex-1x3_lock]
  Power_SW/BAT2_(5VUSB) = Header 2 [package=jst-2-pth]
  Mod1 = Raspberry Pi Pico  # not connected
  Part1 = 9-DOF Absolute Orientation IMU Fusion Breakout - BNO055  # not connected

nets:
  N1: Arduino_Nano.GND, A4988_Board.GND#8, A4988_Board_2.GND#8, JP1.1, Tilt_Servo.3, Pan_Servo.3, Led_Matrix.3, Power_SW/BAT2_(5VUSB).2
  N2: Arduino_Nano.D2, JP1.3
  N3: Arduino_Nano.D3, Tilt_Servo.1
  N4: Arduino_Nano.D4, A4988_Board.MS1, A4988_Board_2.MS1
  N5: Arduino_Nano.D5, A4988_Board.DIR
  N6: Arduino_Nano.D6, A4988_Board.MS2, A4988_Board_2.MS2
  N7: Arduino_Nano.D7, A4988_Board_2.DIR
  N8: Arduino_Nano.D8, A4988_Board.SLEEP, A4988_Board_2.SLEEP
  N9: Arduino_Nano.D9, A4988_Board.STEP
  N10: Arduino_Nano.D10, A4988_Board_2.STEP
  N11: Arduino_Nano.D11/MOSI, Pan_Servo.1
  N12: Arduino_Nano.D12/MISO, Led_Matrix.1
  N13: Arduino_Nano.5V, JP1.6
  N14: Arduino_Nano.A7, JP1.2
  N15: Arduino_Nano.A6, R1.Pin_0, R2.Pin_1
  N16: Arduino_Nano.A5, JP1.4
  N17: Arduino_Nano.A4, JP1.5
  VDD: A4988_Board.RESET, A4988_Board.VDD, A4988_Board_2.RESET, A4988_Board_2.VDD, Tilt_Servo.2, Pan_Servo.2, Led_Matrix.2, Power_SW/BAT2_(5VUSB).1
  N18: A4988_Board.1B, Left_Motor.2
  N19: A4988_Board.1A, Left_Motor.1
  N20: A4988_Board.2A, Left_Motor.4
  N21: A4988_Board.2B, Left_Motor.3
  N22: A4988_Board.GND#14, A4988_Board_2.GND#14, R1.Pin_1, C3.-, C4.-, Power_SW/BAT_(LiPo3S).2
  N23: A4988_Board.VMOT, A4988_Board_2.VMOT, R2.Pin_0, C3.+, C4.+, Power_SW/BAT_(LiPo3S).1
  N24: A4988_Board_2.1B, Right_Motor.2
  N25: A4988_Board_2.1A, Right_Motor.1
  N26: A4988_Board_2.2A, Right_Motor.4
  N27: A4988_Board_2.2B, Right_Motor.3

notes:
  stan
  © 2021 David Beaudette
  Black: GND
  Blue: Gyro analog
  White: Accel data ready
  Magenta: I2C CLK
  Grey: I2C DAT
  Red: 5 V Digital

custom parts:
  Raspberry Pi Pico: Raspberry Pi Pico. Based around the RP2040 microcontroller the Pico is a low cost microcontroller device bringing Raspberry Pi quality, cost, and easy of use to the microcontroller space. Jan 2021, Split part in to two versions: tht (this one) and SMD. This one will drill holes for a .1 in header in pcb to allow plugging in the module as well as providing pads to solder the module to the top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
  9-DOF Absolute Orientation IMU Fusion Breakout - BNO055: A MEMS accelerometer, magnetometer and gyroscope on a single die with a high speed ARM Cortex-M0 based processor to digest all the sensor data, abstract the sensor fusion and real time requirements away, and spit out data you can use in quaternions, Euler angles or vectors.
